# Fritzing sketch EnviroMonitor (saved by Fritzing 0.9.3b)
breadboards: 1

parts:
  WeMos_D1_Mini1 = WeMos D1 Mini
  J2 = female pin header, 2 pins [form="♀ (female)"]  # not connected
  DS1 = DS18B20 1-Wire Temperature Sensor [part_number=DS18B20]
  R1 = Resistor [tolerance=±5% resistance=4.7k package=THT]
  I2C = double row rounded female pin header, 4 pins [form="♀ (female rounded)"]
  PMS = double row rounded female pin header, 6 pins [form="♀ (female rounded)"]
  J3DC = Camdenboss CTB0158-2 [part_number=CTB0158-2 package=THT]
  J4 = Screw terminal - 2 pins [package=THT]  # not connected

nets:
  N1: WeMos_D1_Mini1.3V3, I2C.pin1
  5V: WeMos_D1_Mini1.5V, DS1.VDD, R1.Pin_1, PMS.pin1, J3DC.pin1
  N2: WeMos_D1_Mini1.D1, I2C.pin4
  N3: WeMos_D1_Mini1.D2, I2C.pin3
  N4: WeMos_D1_Mini1.D3, DS1.DQ, R1.Pin_0
  N5: WeMos_D1_Mini1.D5, PMS.pin3
  N6: WeMos_D1_Mini1.D6, PMS.pin5
  N7: WeMos_D1_Mini1.D7, PMS.pin4
  N8: WeMos_D1_Mini1.D8, PMS.pin6
  N9: WeMos_D1_Mini1.G, DS1.GND, I2C.pin2, PMS.pin2, J3DC.pin2

notes:
  12VCC - Cyjan
  5VCC - Czerwony
  3.3VCC - Pomarańczowy
  GND - Czarny
  SDA - Zielony
  SCL - Żółty
  1W data - Biały
  PMS3003 connector (right to left)
  PIN1 - 5VCC
  PIN2 - GND
  PIN3 - SET
  PIN4 - RXD (connect to TX of Wemos)
  PIN5 - TXD (connect to RX of Wemos)
  PIN6 - RST
  I2C connector
  PIN1 - 3.3VCC
  PIN2 - GND
  PIN3 - SDA
  PIN4 - SCL

custom parts:
  WeMos D1 Mini: The D1 mini is a mini wifi board based on ESP-8266EX.
